// Logisim project Proyecto 1.circ as structural Verilog: 13 circuits, main circuit AND
module AND (
  input  a,
  input  b,
  output out
);

  wire and_1_out;

  and and_1 (and_1_out, a, b);
  not not_1 (out, and_1_out);

  // Notes on the sheet:
  //   outNand
endmodule

module OR (
  input  a,
  input  b,
  output out_3
);

  wire and_1_out, not_1_out, not_2_out;

  not not_1 (not_1_out, a);
  not not_2 (not_2_out, b);
  and and_1 (and_1_out, not_1_out, not_2_out);
  not not_3 (out_3, and_1_out);
endmodule

module NOT (
  input  in_1,
  output out_2
);

  not not_1 (out_2, in_1);
endmodule

module XOR (
  input  a,
  input  b,
  output out_3
);

  wire and_1_out, and_2_out, not_1_out, not_2_out;

  not not_1 (not_1_out, a);
  not not_2 (not_2_out, b);
  and and_1 (and_1_out, not_1_out, b);
  and and_2 (and_2_out, a, not_2_out);
  or or_1 (out_3, and_1_out, and_2_out);
endmodule

module MUX (
  input  a,
  input  sel,
  input  b,
  output out
);

  wire and_1_out, and_2_out, not_1_out;

  not not_1 (not_1_out, sel);
  and and_1 (and_1_out, a, not_1_out);
  and and_2 (and_2_out, sel, b);
  or or_1 (out, and_1_out, and_2_out);
endmodule

module DMUX (
  input  Sel,
  input  in,
  output a,
  output b
);

  wire not_1_out;

  not not_1 (not_1_out, Sel);
  and and_1 (a, Sel, in);
  and and_2 (b, in, not_1_out);
endmodule

module AND16 (
  input  [15:0] a,
  input  [15:0] b,
  output [15:0] out
);

  assign out = a & b;  // AND_Gate and_1, 16 bits wide
endmodule

module OR16 (
  input  [15:0] a,
  input  [15:0] b,
  output [15:0] out
);

  assign out = a | b;  // OR_Gate or_1, 16 bits wide
endmodule

module MUX16 (
  input  [15:0] a,
  input  [15:0] b,
  input  sel,
  output [15:0] out
);

  Multiplexer #(.width(16)) multiplexer_1 (.in0(a), .in1(b), .out(out), .sel(sel));  // open: en
endmodule

module Or8Way (
  input  _0,
  input  _1,
  input  _2,
  input  _3,
  input  _4,
  input  _5,
  input  _6,
  input  _7,
  output out
);

  wire a_out, b_out, c_out, d_out, e_out, f_out;

  or a (a_out, _0, _1);
  or b (b_out, _2, _3);
  or c (c_out, _4, _5);
  or d (d_out, _6, _7);
  or e (e_out, a_out, b_out);
  or f (f_out, c_out, d_out);
  or g (out, e_out, f_out);
endmodule

module Mux4Way16 (
  input  [15:0] a,
  input  [15:0] b,
  input  sel,
  input  sel_2,
  input  [15:0] c,
  input  [15:0] d,
  input  sel_3,
  output [15:0] out
);

  wire [15:0] mux16_1_out, mux16_2_out;

  MUX16 mux16_1 (.a(a), .b(b), .sel(sel), .out(mux16_1_out));
  MUX16 mux16_2 (.a(c), .b(d), .sel(sel_3), .out(mux16_2_out));
  MUX16 mux16_3 (.a(mux16_1_out), .b(mux16_2_out), .sel(sel_2), .out(out));
endmodule

module Mux8Way16 (
  input  [15:0] a,
  input  [15:0] b,
  input  [15:0] c,
  input  [15:0] d,
  input  [2:0] sel,
  input  [15:0] e,
  input  [15:0] f,
  input  [15:0] g,
  input  [15:0] h,
  output [15:0] out
);

  wire [15:0] multiplexer_1_out, multiplexer_2_out, mux16_1_out, mux16_2_out, mux16_3_out, mux16_4_out;

  MUX16 mux16_1 (.a(a), .b(b), .sel(sel[0]), .out(mux16_1_out));
  MUX16 mux16_2 (.a(c), .b(d), .sel(sel[0]), .out(mux16_2_out));
  MUX16 mux16_3 (.a(e), .b(f), .sel(sel[0]), .out(mux16_3_out));
  MUX16 mux16_4 (.a(g), .b(h), .sel(sel[0]), .out(mux16_4_out));
  Multiplexer #(.width(16)) multiplexer_1 (
    .in0(mux16_1_out), .in1(mux16_2_out), .out(multiplexer_1_out), .sel(sel[1]));  // open: en
  Multiplexer #(.width(16)) multiplexer_2 (
    .in0(mux16_3_out), .in1(mux16_4_out), .out(multiplexer_2_out), .sel(sel[1]));  // open: en
  Multiplexer #(.width(16)) multiplexer_3 (
    .in0(multiplexer_1_out), .in1(multiplexer_2_out), .out(out), .sel(sel[2]));  // open: en
endmodule

module DMux4Way (
  input  in,
  input  [1:0] sel,
  output a,
  output b,
  output c,
  output d
);

  wire demultiplexer_1_out0;

  Demultiplexer demultiplexer_1 (.out0(demultiplexer_1_out0), .in(in), .sel(sel[1]));  // open: out1, en
  Demultiplexer demultiplexer_2 (.out0(a), .out1(b), .in(demultiplexer_1_out0), .sel(sel[0]));  // open: en
  Demultiplexer demultiplexer_3 (.out0(c), .out1(d), .sel(sel[0]));  // open: in, en
endmodule
