// Logisim project Proyecto 2.circ as structural Verilog: 4 circuits, main circuit Half Adder
module Full_Adder (
  input  a,
  input  b,
  input  Carry_in,
  output sum,
  output Carry_out
);

  wire and_1_out, and_2_out, xor_1_out;

  xor xor_1 (xor_1_out, a, b);
  and and_1 (and_1_out, a, b);
  and and_2 (and_2_out, xor_1_out, Carry_in);
  xor xor_2 (sum, xor_1_out, Carry_in);
  or or_1 (Carry_out, and_1_out, and_2_out);
endmodule

module Half_Adder (
  input  a,
  input  b,
  output sum,
  output carry
);

  xor xor_1 (sum, a, b);
  and and_1 (carry, a, b);
endmodule

module ADD16 (
  input  [15:0] a,
  input  [15:0] b,
  output [15:0] sum
);

  Half_Adder half_adder_1 (.a(a[0]), .b(b[0]), .sum(sum[0]));  // open: carry
endmodule

module ALU (
  input  [15:0] x,
  input  zx,
  input  nx,
  input  f,
  input  [15:0] y,
  input  zy,
  input  ny,
  input  no,
  output [15:0] out,
  output out_10,
  output ng
);

  wire or_1_out;
  wire [15:0] add16_1_sum, and_1_out, multiplexer_2_out, multiplexer_3_out, multiplexer_4_out,
       multiplexer_5_out, multiplexer_6_out, not_1_out, not_2_out, not_3_out;

  assign not_1_out = ~multiplexer_6_out;  // NOT_Gate not_1, 16 bits wide
  Multiplexer #(.width(16)) multiplexer_1 (
    .in0(multiplexer_6_out), .in1(not_1_out), .out({ng, out[14:0]}), .sel(no));  // open: en
  Multiplexer #(.width(16)) multiplexer_2 (.in0(x), .in1({16{1'b0}}), .out(multiplexer_2_out), .sel(zx));  // open: en
  Multiplexer #(.width(16)) multiplexer_3 (.in0(y), .in1({16{1'b0}}), .out(multiplexer_3_out), .sel(zy));  // open: en
  assign not_2_out = ~multiplexer_2_out;  // NOT_Gate not_2, 16 bits wide
  assign not_3_out = ~multiplexer_3_out;  // NOT_Gate not_3, 16 bits wide
  Multiplexer #(.width(16)) multiplexer_4 (
    .in0(multiplexer_2_out), .in1(not_2_out), .out(multiplexer_4_out), .sel(nx));  // open: en
  Multiplexer #(.width(16)) multiplexer_5 (
    .in0(multiplexer_3_out), .in1(not_3_out), .out(multiplexer_5_out), .sel(ny));  // open: en
  assign and_1_out = multiplexer_4_out & multiplexer_5_out;  // AND_Gate and_1, 16 bits wide
  ADD16 add16_1 (.a(multiplexer_4_out), .b(multiplexer_5_out), .sum(add16_1_sum));
  Multiplexer #(.width(16)) multiplexer_6 (
    .in0(and_1_out), .in1(add16_1_sum), .out(multiplexer_6_out), .sel(f));  // open: en
  or or_1 (or_1_out, out[0], out[1], out[2], out[3], out[4], out[5], out[6], out[7], out[8], out[9], out[10], out[11], out[12], out[13], out[14], ng);
  not not_4 (out_10, or_1_out);

  assign out[15] = ng;
endmodule
