// Logisim project Proyecto 3.circ as structural Verilog: 2 circuits, main circuit Bit
module Bit (
  input  in,
  input  load,
  output out
);

  wire clock_1_out, multiplexer_1_out;

  Clock clock_1 (.out(clock_1_out));
  Multiplexer multiplexer_1 (.in0(out), .in1(in), .out(multiplexer_1_out), .sel(load));  // open: en
  D_Flip_Flop d_ff_1 (.clk(clock_1_out), .D(multiplexer_1_out), .Qn(out));  // open: Q, preset, en, reset
endmodule

module Register (
  input  [15:0] in_1,
  input  load,
  output [15:0] out_3
);

  wire clock_1_out;
  wire [15:0] multiplexer_1_out;

  Multiplexer #(.width(16)) multiplexer_1 (.in0(out_3), .in1(in_1), .out(multiplexer_1_out), .sel(load));  // open: en
  Register_part #(.width(16)) register_1 (.D(multiplexer_1_out), .Q(out_3), .clk(clock_1_out));  // open: en, clr
  Clock clock_1 (.out(clock_1_out));
endmodule
